// Logisim project 18105226_陈宇卿.circ as structural Verilog: 8 circuits, main circuit main
module main (
);

  _18105226_IFU u_18105226_ifu_1 ();
endmodule

module _18105226_IFU (
);

  Register #(.width(32), .trigger("rising"), .Select("low")) PC ();  // open: D, en, Q, clk, clr
endmodule

// 4bits ADD
module _18105226_4bit_ADDU (
  input  C0,
  input  A0,
  input  B0,
  input  A1,
  input  B1,
  input  A2,
  input  B2,
  input  A3,
  input  B3,
  output Sigma0,
  output Sigma1,
  output Sigma2,
  output Sigma3,
  output P0_star,
  output G0_star
);

  wire and_1_out, and_2_out, and_3_out, and_4_out, and_5_out, and_6_out, and_7_out, and_8_out, and_9_out,
       C1_out, C2_out, C3_out, G0, G1, G2, G3, P0, P1, P2, P3;

  and u_G0 (G0, A0, B0);
  xor u_P0 (P0, A0, B0);
  and u_G1 (G1, A1, B1);
  xor u_P1 (P1, A1, B1);
  and u_G2 (G2, A2, B2);
  xor u_P2 (P2, A2, B2);
  and u_G3 (G3, A3, B3);
  xor u_P3 (P3, A3, B3);
  xor u_Sigma0 (Sigma0, C0, P0);
  and and_1 (and_1_out, C0, P0);
  and and_2 (and_2_out, P1, G0);
  and and_3 (and_3_out, C0, P0, P1);
  and and_4 (and_4_out, G1, P2);
  and and_5 (and_5_out, P2, P1, G0);
  and and_6 (and_6_out, P2, P1, P0, C0);
  and and_7 (and_7_out, P3, G2);
  and and_8 (and_8_out, P3, P2, G1);
  and and_9 (and_9_out, P3, P2, P1, G0);
  or C1 (C1_out, and_1_out, G0);
  or C2 (C2_out, G1, and_2_out, and_3_out);
  or C3 (C3_out, G2, and_4_out, and_5_out, and_6_out);
  and and_10 (P0_star, P0, P1, P2, P3);
  or or_1 (G0_star, G3, and_7_out, and_8_out, and_9_out);
  xor u_Sigma1 (Sigma1, C1_out, P1);
  xor u_Sigma2 (Sigma2, C2_out, P2);
  xor u_Sigma3 (Sigma3, P3, C3_out);
endmodule

// 16bits Parallel Carry Link
module _18105226_Parallel_Carry_Link (
  input  C0,
  input  P0_star,
  input  G0_star,
  input  G1_star,
  input  P1_star,
  input  G2_star,
  input  P2_star,
  input  G3_star,
  input  P3_star,
  output C4,
  output C8,
  output C12,
  output C16
);

  wire and_1_out, and_2_out, and_3_out, and_4_out, and_5_out, and_6_out, and_7_out, and_8_out, and_9_out,
       nand_1_out, nor_1_out;

  and and_1 (and_1_out, C0, P0_star);
  and and_2 (and_2_out, C0, P0_star, P1_star);
  and and_3 (and_3_out, G0_star, P1_star);
  and and_4 (and_4_out, C0, P0_star, P1_star, P2_star);
  and and_5 (and_5_out, G0_star, P1_star, P2_star);
  and and_6 (and_6_out, G1_star, P2_star);
  and and_7 (and_7_out, G0_star, P1_star, P2_star, P3_star);
  and and_8 (and_8_out, G1_star, P2_star, P3_star);
  and and_9 (and_9_out, G2_star, P3_star);
  or or_1 (C4, and_1_out, G0_star);
  or or_2 (C8, and_2_out, and_3_out, G1_star);
  or or_3 (C12, and_4_out, and_5_out, and_6_out, G2_star);
  nor nor_1 (nor_1_out, and_7_out, and_8_out, and_9_out, G3_star);
  nand nand_1 (nand_1_out, C0, P0_star, P1_star, P2_star, P3_star);
  nand nand_2 (C16, nor_1_out, nand_1_out);
endmodule

// 16bits ADD
module _18105226_16bits_ADDU (
  input  [15:0] A_15_0,
  input  C0,
  input  [15:0] B_15_0,
  output C16,
  output [15:0] AddOut_15_0
);

  wire C4, C8, C12, n18105226_4bit_addu_1_g0_star, n18105226_4bit_addu_1_p0_star,
       n18105226_4bit_addu_2_g0_star, n18105226_4bit_addu_2_p0_star, n18105226_4bit_addu_3_g0_star,
       n18105226_4bit_addu_3_p0_star, n18105226_4bit_addu_4_g0_star, n18105226_4bit_addu_4_p0_star;

  _18105226_4bit_ADDU u_18105226_4bit_addu_1 (
    .C0(C0), .A0(A_15_0[0]), .B0(B_15_0[0]), .A1(A_15_0[1]), .B1(B_15_0[1]), .A2(A_15_0[2]), .B2(B_15_0[2]),
    .A3(A_15_0[3]), .B3(B_15_0[3]), .Sigma0(AddOut_15_0[0]), .Sigma1(AddOut_15_0[1]),
    .Sigma2(AddOut_15_0[2]), .Sigma3(AddOut_15_0[3]), .P0_star(n18105226_4bit_addu_1_p0_star),
    .G0_star(n18105226_4bit_addu_1_g0_star));
  _18105226_4bit_ADDU u_18105226_4bit_addu_2 (
    .C0(C4), .A0(A_15_0[4]), .B0(B_15_0[4]), .A1(A_15_0[5]), .B1(B_15_0[5]), .A2(A_15_0[6]), .B2(B_15_0[6]),
    .A3(A_15_0[7]), .B3(B_15_0[7]), .Sigma0(AddOut_15_0[4]), .Sigma1(AddOut_15_0[5]),
    .Sigma2(AddOut_15_0[6]), .Sigma3(AddOut_15_0[7]), .P0_star(n18105226_4bit_addu_2_p0_star),
    .G0_star(n18105226_4bit_addu_2_g0_star));
  _18105226_4bit_ADDU u_18105226_4bit_addu_3 (
    .C0(C8), .A0(A_15_0[8]), .B0(B_15_0[8]), .A1(A_15_0[9]), .B1(B_15_0[9]), .A2(A_15_0[10]),
    .B2(B_15_0[10]), .A3(A_15_0[11]), .B3(B_15_0[11]), .Sigma0(AddOut_15_0[8]), .Sigma1(AddOut_15_0[9]),
    .Sigma2(AddOut_15_0[10]), .Sigma3(AddOut_15_0[11]), .P0_star(n18105226_4bit_addu_3_p0_star),
    .G0_star(n18105226_4bit_addu_3_g0_star));
  _18105226_4bit_ADDU u_18105226_4bit_addu_4 (
    .C0(C12), .A0(A_15_0[12]), .B0(B_15_0[12]), .A1(A_15_0[13]), .B1(B_15_0[13]), .A2(A_15_0[14]),
    .B2(B_15_0[14]), .A3(A_15_0[15]), .B3(B_15_0[15]), .Sigma0(AddOut_15_0[12]), .Sigma1(AddOut_15_0[13]),
    .Sigma2(AddOut_15_0[14]), .Sigma3(AddOut_15_0[15]), .P0_star(n18105226_4bit_addu_4_p0_star),
    .G0_star(n18105226_4bit_addu_4_g0_star));
  _18105226_Parallel_Carry_Link u_18105226_parallel_carry_link_1 (
    .C0(C0), .P0_star(n18105226_4bit_addu_1_p0_star), .G0_star(n18105226_4bit_addu_1_g0_star),
    .G1_star(n18105226_4bit_addu_2_g0_star), .P1_star(n18105226_4bit_addu_2_p0_star),
    .G2_star(n18105226_4bit_addu_3_g0_star), .P2_star(n18105226_4bit_addu_3_p0_star),
    .G3_star(n18105226_4bit_addu_4_g0_star), .P3_star(n18105226_4bit_addu_4_p0_star), .C4(C4), .C8(C8),
    .C12(C12), .C16(C16));

  // Other names for the same wires on the sheet: A_3_0[3:0] = A_15_0[3:0]; A_7_4[3:0] = A_15_0[7:4];
  //   A_11_8[3:0] = A_15_0[11:8]; A_15_12[3:0] = A_15_0[15:12]; B_3_0[3:0] = B_15_0[3:0]; B_7_4[3:0] = B_15_0[7:4];
  //   B_11_8[3:0] = B_15_0[11:8]; B_15_12[3:0] = B_15_0[15:12]
endmodule

// 32bits ADDU
module _18105226_32bits_ADDU (
  input  [31:0] A_31_0,
  input  [31:0] B_31_0,
  output [31:0] AddOut_31_0
);

  wire n18105226_16bits_addu_1_c16;

  _18105226_16bits_ADDU u_18105226_16bits_addu_1 (
    .A_15_0(A_31_0[15:0]), .C0(1'b0), .B_15_0(B_31_0[15:0]), .C16(n18105226_16bits_addu_1_c16),
    .AddOut_15_0(AddOut_31_0[15:0]));
  _18105226_16bits_ADDU u_18105226_16bits_addu_2 (
    .A_15_0(A_31_0[31:16]), .C0(n18105226_16bits_addu_1_c16), .B_15_0(B_31_0[31:16]),
    .AddOut_15_0(AddOut_31_0[31:16]));  // open: C16
endmodule

// 32bits SUBU
module _18105226_32bits_SUBU (
  input  [31:0] A_31_0,
  input  [31:0] B_31_0,
  output [31:0] AddOut_31_0
);

  wire n18105226_16bits_addu_1_c16;
  wire [31:0] not_1_out;

  assign not_1_out = ~B_31_0;  // NOT_Gate not_1, 32 bits wide
  _18105226_16bits_ADDU u_18105226_16bits_addu_1 (
    .A_15_0(A_31_0[15:0]), .C0(1'b1), .B_15_0(not_1_out[15:0]), .C16(n18105226_16bits_addu_1_c16),
    .AddOut_15_0(AddOut_31_0[15:0]));
  _18105226_16bits_ADDU u_18105226_16bits_addu_2 (
    .A_15_0(A_31_0[31:16]), .C0(n18105226_16bits_addu_1_c16), .B_15_0(not_1_out[31:16]),
    .AddOut_15_0(AddOut_31_0[31:16]));  // open: C16
endmodule

// ALU
module _18105226_ALU (
  input  [1:0] ALUctr,
  input  [31:0] Source0,
  input  [31:0] Source1,
  output ZERO,
  output [31:0] ALUout
);

  wire [31:0] n18105226_32bits_addu_1_addout_31_0, n18105226_32bits_subu_1_addout_31_0, ORI_out;

  _18105226_32bits_ADDU u_18105226_32bits_addu_1 (
    .A_31_0(Source0), .B_31_0(Source1), .AddOut_31_0(n18105226_32bits_addu_1_addout_31_0));
  _18105226_32bits_SUBU u_18105226_32bits_subu_1 (
    .A_31_0(Source0), .B_31_0(Source1), .AddOut_31_0(n18105226_32bits_subu_1_addout_31_0));
  assign ORI_out = Source0 | Source1;  // OR_Gate ORI, 32 bits wide
  Multiplexer #(.select(2), .width(32), .disabled("Z"), .enable("false")) multiplexer_1 (
    .in0(n18105226_32bits_addu_1_addout_31_0), .in1(n18105226_32bits_subu_1_addout_31_0), .in2(ORI_out),
    .out(ALUout), .sel(ALUctr));  // open: in3
  nor nor_1 (ZERO, n18105226_32bits_subu_1_addout_31_0[0], n18105226_32bits_subu_1_addout_31_0[1], n18105226_32bits_subu_1_addout_31_0[2], n18105226_32bits_subu_1_addout_31_0[3], n18105226_32bits_subu_1_addout_31_0[4], n18105226_32bits_subu_1_addout_31_0[5], n18105226_32bits_subu_1_addout_31_0[6], n18105226_32bits_subu_1_addout_31_0[7], n18105226_32bits_subu_1_addout_31_0[8], n18105226_32bits_subu_1_addout_31_0[9], n18105226_32bits_subu_1_addout_31_0[10], n18105226_32bits_subu_1_addout_31_0[11], n18105226_32bits_subu_1_addout_31_0[12], n18105226_32bits_subu_1_addout_31_0[13], n18105226_32bits_subu_1_addout_31_0[14], n18105226_32bits_subu_1_addout_31_0[15], n18105226_32bits_subu_1_addout_31_0[17], n18105226_32bits_subu_1_addout_31_0[18], n18105226_32bits_subu_1_addout_31_0[19], n18105226_32bits_subu_1_addout_31_0[20], n18105226_32bits_subu_1_addout_31_0[21], n18105226_32bits_subu_1_addout_31_0[22], n18105226_32bits_subu_1_addout_31_0[23], n18105226_32bits_subu_1_addout_31_0[24], n18105226_32bits_subu_1_addout_31_0[25], n18105226_32bits_subu_1_addout_31_0[26], n18105226_32bits_subu_1_addout_31_0[27], n18105226_32bits_subu_1_addout_31_0[28], n18105226_32bits_subu_1_addout_31_0[29], n18105226_32bits_subu_1_addout_31_0[30], n18105226_32bits_subu_1_addout_31_0[31], n18105226_32bits_subu_1_addout_31_0[16]);

  // Notes on the sheet:
  //   00-ADDU 01-SUBU 10-ORI
endmodule
